// Logisim project Д8423.circ as structural Verilog: 1 circuit, main circuit main
module main (
  input  [3:0] in_1
);

  wire and_1_out, and_2_out, and_4_out, and_5_out, not_1_out, not_2_out, not_3_out, not_4_out, not_5_out,
       not_6_out, not_7_out, not_8_out, not_9_out, not_10_out;
  wire [3:0] or_1_out;

  // Probe on or_1_out
  not not_1 (not_1_out, in_1[1]);
  not not_2 (not_2_out, in_1[2]);
  not not_3 (not_3_out, in_1[3]);
  and and_1 (and_1_out, not_1_out, in_1[0], not_2_out);
  and and_2 (and_2_out, not_3_out, in_1[0]);
  or or_1 (or_1_out[0], and_1_out, and_2_out);
  not not_4 (not_4_out, in_1[3]);
  not not_5 (not_5_out, in_1[1]);
  and and_3 (or_1_out[1], not_4_out, not_5_out);
  not not_6 (not_6_out, in_1[3]);
  not not_7 (not_7_out, in_1[2]);
  not not_8 (not_8_out, in_1[3]);
  not not_9 (not_9_out, in_1[1]);
  and and_4 (and_4_out, not_6_out, not_7_out, in_1[1]);
  and and_5 (and_5_out, not_8_out, in_1[2], not_9_out);
  or or_2 (or_1_out[2], and_4_out, and_5_out);
  not not_10 (not_10_out, in_1[3]);
  and and_6 (or_1_out[3], in_1[2], not_10_out, in_1[1]);
endmodule
